// Logisim project cache1.circ as structural Verilog: 1 circuit, main circuit main
module main (
);

  wire and_1_out, and_2_out, and_3_out, d_ff_1_q, not_1_out, not_2_out, not_3_out, or_1_out,
       transmission_1_p4, undriven, undriven_2, undriven_3;

  not not_1 (not_1_out, undriven);
  not not_2 (not_2_out, undriven_3);
  or or_1 (or_1_out, not_1_out, undriven_2);
  and and_1 (and_1_out, not_2_out, or_1_out);
  and and_2 (and_2_out, not_2_out, transmission_1_p4);
  and and_3 (and_3_out, not_2_out, undriven, undriven_2);
  D_Flip_Flop #(.trigger("high")) d_ff_1 (.clk(and_1_out), .D(and_2_out), .Q(d_ff_1_q));  // open: Qn, preset, en, reset
  not not_3 (not_3_out, and_3_out);
  // Transmission_Gate transmission_1: pin names not known; wires that end beside it: d_ff_1_q, not_3_out, and_3_out, transmission_1_p4

  // Notes on the sheet:
  //   Enable
  //   RD_WR
  //   Data
  //   Reset
endmodule
